// Logisim project BeEight.circ as structural Verilog: 1 circuit, main circuit main
module main (
  input  Device0,
  input  in_2,
  input  Device1,
  input  in_4,
  input  Device2,
  input  in_6,
  input  Device3
);

  wire and_2_out, and_3_out, and_4_out, and_5_out, and_6_out, and_8_out, and_9_out, Carry, CLK, CLKIN,
       ConditionalFlag, ConditionalResult, controlled_buffer_10_out, controlled_buffer_11_out,
       controlled_buffer_13_out, controlled_buffer_14_out, controlled_buffer_15_out,
       controlled_buffer_16_out, controlled_buffer_17_out, controlled_buffer_18_out,
       controlled_buffer_19_out, Equal, ia, ialu, im, Inst0, ipb, ipc, ipcs, isb, n74138_1_pin4,
       n74138_1_pin5, n74138_1_pin6, n74138_1_pin7, n74138_1_pin9, n74138_1_pin10, n74138_1_pin11,
       n74138_1_pin12, n74138_1_pin13, n74138_1_pin14, n74138_1_pin15, nInst0, not_1_out, not_2_out,
       not_3_out, not_4_out, not_5_out, not_6_out, not_7_out, not_8_out, not_9_out, not_10_out, not_11_out,
       not_12_out, not_13_out, not_14_out, not_16_out, nxt, oa, oalu, om, opb, opc, opcs, or_1_out, or_2_out,
       or_3_out, osb, pull_resistor_2_node, s_r_ff_1_qn, special, ucf, xnor_1_out, xnor_2_out, xnor_3_out,
       xnor_4_out, xnor_5_out, xnor_6_out, xnor_7_out, xnor_8_out, Zero;
  wire [3:0] Condition, controlled_buffer_4_out, InstructionCounter, pull_resistor_1_node;
  wire [3:1] Instruction;
  wire [6:0] rom_1_data;
  wire [7:0] Accumulator, adder_1_out, ALU, ALUin, Databus, nand_1_out, SecondaryBuffer;
  wire [7:4] ProgramCounterStorageUpper_q;
  wire [11:0] Address, StoredAddress;
  wire [11:8] Databus12;

  S_R_Flip_Flop s_r_ff_1 (.reset(in_6), .Qn(s_r_ff_1_qn), .preset(in_4));  // open: S, R, clk, Q
  and and_1 (CLK, s_r_ff_1_qn, CLKIN);
  and and_2 (and_2_out, osb, Inst0, Instruction[1], Instruction[2]);
  not not_1 (not_1_out, and_2_out);
  and and_3 (and_3_out, and_2_out, ConditionalFlag);
  Pull_Resistor pull_resistor_1 (.node(pull_resistor_1_node));
  or or_1 (or_1_out, not_1_out, and_3_out);
  Register ProgramCounterStorageLower (.D(Databus), .en(ipcs), .clk(CLK), .Q(StoredAddress[7:0]), .clr(in_2));
  Register ProgramCounterStorageUpper (
    .D({pull_resistor_1_node, Databus12}), .en(ipcs), .clk(CLK),
    .Q({ProgramCounterStorageUpper_q, StoredAddress[11:8]}), .clr(in_2));
  and and_4 (and_4_out, CLK, or_1_out, ipc);
  Counter #(.max('hfff), .width(12)) ProgramCounter (
    .clr(in_2), .load(not_2_out), .up(1'b1), .count(special), .clk(and_4_out), .D({Databus12, Databus}),
    .Q(Address));  // open: carry
  not not_2 (not_2_out, special);
  assign {Databus12, Databus} = and_5_out ? StoredAddress : 12'bz;  // Controlled_Buffer controlled_buffer_1
  and and_5 (and_5_out, opcs, not_3_out);
  not not_3 (not_3_out, special);
  assign Databus = and_6_out ? {ProgramCounterStorageUpper_q, StoredAddress[11:8]} : 8'bz;  // Controlled_Buffer controlled_buffer_2
  and and_6 (and_6_out, opcs, special);
  assign {Databus12, Databus} = opc ? Address : 12'bz;  // Controlled_Buffer controlled_buffer_3
  Hex_Digit_Display #(.decimalPoint("false")) hex_digit_display_1 (.value({Instruction, Inst0}));
  Hex_Digit_Display #(.decimalPoint("false")) hex_digit_display_2 (.value(Address[7:4]));
  Hex_Digit_Display #(.decimalPoint("false")) hex_digit_display_3 (.value(Address[11:8]));
  Hex_Digit_Display #(.decimalPoint("false")) hex_digit_display_4 (.value(Databus12));
  Hex_Digit_Display #(.decimalPoint("false")) hex_digit_display_5 (.value(InstructionCounter));
  or or_2 (or_2_out, in_2, nxt);
  ROM rom_1 (.addr({Instruction, Inst0, InstructionCounter}), .data({nxt, rom_1_data[6:4], special, rom_1_data[2:0]}));
  assign controlled_buffer_4_out = special ? {Instruction, Inst0} : 4'bz;  // Controlled_Buffer controlled_buffer_4
  not not_4 (not_4_out, special);
  assign controlled_buffer_4_out = not_4_out ? Databus[3:0] : 4'bz;  // Controlled_Buffer controlled_buffer_5
  Hex_Digit_Display #(.decimalPoint("false")) hex_digit_display_6 (.value(Address[3:0]));
  Hex_Digit_Display #(.decimalPoint("false")) hex_digit_display_7 (.value(Accumulator[7:4]));
  Hex_Digit_Display #(.decimalPoint("false")) hex_digit_display_8 (.value(Databus[7:4]));
  Hex_Digit_Display #(.decimalPoint("false")) hex_digit_display_9 (.value(Databus[3:0]));
  Counter #(.max('hf), .trigger("falling"), .width(4)) counter_1 (
    .clr(or_2_out), .load(1'b0), .up(1'b1), .count(1'b1), .clk(CLK), .Q(InstructionCounter));  // open: D, carry
  Register PrimaryBuffer (
    .D({Databus[7:4], controlled_buffer_4_out}), .en(ipb), .clk(CLK), .Q({Instruction, Inst0, Condition}));  // open: clr
  Register u_SecondaryBuffer (.D(Databus), .en(isb), .clk(CLK), .Q(SecondaryBuffer));  // open: clr
  Hex_Digit_Display #(.decimalPoint("false")) hex_digit_display_10 (.value(Accumulator[3:0]));
  Hex_Digit_Display #(.decimalPoint("false")) hex_digit_display_11 (.value({Instruction, Inst0}));
  Clock clock_1 (.out(CLKIN));
  RAM #(.addrWidth(12), .databus("bidir"), .trigger("high"), .\type ("nonvolatile")) ram_1 (
    .addr(Address), .we(im), .oe(om), .data(Databus));
  assign Databus = osb ? SecondaryBuffer : 8'bz;  // Controlled_Buffer controlled_buffer_6
  assign {Databus12, Databus} = osb ? {Condition, SecondaryBuffer} : 12'bz;  // Controlled_Buffer controlled_buffer_7
  Hex_Digit_Display #(.decimalPoint("false")) hex_digit_display_12 (.value(ALU[7:4]));
  Hex_Digit_Display #(.decimalPoint("false")) hex_digit_display_13 (.value(ALU[3:0]));
  Hex_Digit_Display #(.decimalPoint("false")) hex_digit_display_14 (.value(Condition));
  Hex_Digit_Display #(.decimalPoint("false")) hex_digit_display_15 (.value(SecondaryBuffer[7:4]));
  LED led_1 (.in(om));
  LED led_2 (.in(opb));
  LED led_3 (.in(im));
  LED led_4 (.in(ipb));
  Hex_Digit_Display #(.decimalPoint("false")) hex_digit_display_16 (.value(SecondaryBuffer[3:0]));
  Hex_Digit_Display #(.decimalPoint("false")) hex_digit_display_17 (.value(StoredAddress[11:8]));
  Demultiplexer #(.select(3)) demultiplexer_1 (
    .out1(im), .out2(ipb), .out3(isb), .out4(ia), .out5(ialu), .out6(ipc), .out7(ipcs), .in(1'b1),
    .sel(rom_1_data[2:0]));  // open: out0
  Demultiplexer #(.select(3)) demultiplexer_2 (
    .out1(om), .out2(opb), .out3(osb), .out4(oa), .out5(oalu), .out6(opc), .out7(opcs), .in(1'b1),
    .sel(rom_1_data[6:4]));  // open: out0
  LED led_5 (.in(osb));
  LED led_6 (.in(oa));
  LED led_7 (.in(isb));
  LED led_8 (.in(ia));
  Hex_Digit_Display #(.decimalPoint("false")) hex_digit_display_18 (.value(StoredAddress[7:4]));
  Hex_Digit_Display #(.decimalPoint("false")) hex_digit_display_19 (.value(StoredAddress[3:0]));
  Register u_Accumulator (.D(Databus), .en(ia), .clk(CLK), .Q(Accumulator));  // open: clr
  Register ALUbuffer (.D(ALUin), .en(ialu), .clk(CLK), .Q(ALU));  // open: clr
  LED led_9 (.in(oalu));
  LED led_10 (.in(opc));
  LED led_11 (.in(ialu));
  LED led_12 (.in(ipc));
  LED led_13 (.in(special));
  LED led_14 (.in(nxt));
  assign Databus = oa ? Accumulator : 8'bz;  // Controlled_Buffer controlled_buffer_8
  assign Databus = oalu ? ALU : 8'bz;  // Controlled_Buffer controlled_buffer_9
  LED led_15 (.in(opcs));
  LED led_16 (.in(ipcs));
  LED led_17 (.in(CLK));
  LED led_18 (.in(ConditionalFlag));
  LED RD (.in(om));
  LED WR (.in(im));
  and and_7 (ucf, ialu, special);
  _74138 #(.ShowInternalStructure("true")) u_74138_1 (
    .pin1(Condition[1]), .pin2(Condition[2]), .pin3(Condition[3]), .pin4(n74138_1_pin4),
    .pin5(n74138_1_pin5), .pin6(n74138_1_pin6), .pin7(n74138_1_pin7), .pin15(n74138_1_pin15),
    .pin14(n74138_1_pin14), .pin13(n74138_1_pin13), .pin12(n74138_1_pin12), .pin11(n74138_1_pin11),
    .pin10(n74138_1_pin10), .pin9(n74138_1_pin9));
  not not_5 (not_5_out, n74138_1_pin15);
  Pull_Resistor #(.pull(1)) pull_resistor_2 (.node(pull_resistor_2_node));
  assign controlled_buffer_10_out = not_5_out ? pull_resistor_2_node : 1'bz;  // Controlled_Buffer controlled_buffer_10
  not not_6 (not_6_out, n74138_1_pin14);
  assign controlled_buffer_11_out = not_7_out ? Carry : 1'bz;  // Controlled_Buffer controlled_buffer_11
  not not_7 (not_7_out, ucf);
  assign controlled_buffer_11_out = ucf ? ConditionalResult : 1'bz;  // Controlled_Buffer controlled_buffer_12
  assign controlled_buffer_13_out = not_6_out ? Zero : 1'bz;  // Controlled_Buffer controlled_buffer_13
  not not_8 (not_8_out, n74138_1_pin13);
  assign controlled_buffer_14_out = not_8_out ? Equal : 1'bz;  // Controlled_Buffer controlled_buffer_14
  not not_9 (not_9_out, n74138_1_pin12);
  assign controlled_buffer_15_out = not_9_out ? Accumulator[7] : 1'bz;  // Controlled_Buffer controlled_buffer_15
  not not_10 (not_10_out, n74138_1_pin11);
  assign controlled_buffer_16_out = not_10_out ? Device0 : 1'bz;  // Controlled_Buffer controlled_buffer_16
  not not_11 (not_11_out, n74138_1_pin10);
  Register #(.width(1)) register_1 (
    .D(controlled_buffer_11_out), .en(ialu), .clk(CLK), .Q(ConditionalFlag));  // open: clr
  assign controlled_buffer_17_out = not_11_out ? Device1 : 1'bz;  // Controlled_Buffer controlled_buffer_17
  not not_12 (not_12_out, n74138_1_pin9);
  assign controlled_buffer_18_out = not_12_out ? Device2 : 1'bz;  // Controlled_Buffer controlled_buffer_18
  not not_13 (not_13_out, n74138_1_pin7);
  assign controlled_buffer_19_out = not_13_out ? Device3 : 1'bz;  // Controlled_Buffer controlled_buffer_19
  assign ALUin = nInst0 ? adder_1_out : 8'bz;  // Controlled_Buffer controlled_buffer_20
  Adder adder_1 (.a(Accumulator), .b(SecondaryBuffer), .out(adder_1_out), .cin(ConditionalFlag), .cout(Carry));
  assign nand_1_out = ~(Accumulator & SecondaryBuffer);  // NAND_Gate nand_1, 8 bits wide
  assign ALUin = Inst0 ? nand_1_out : 8'bz;  // Controlled_Buffer controlled_buffer_21
  Pull_Resistor pull_resistor_3 (.node(controlled_buffer_10_out));
  Pull_Resistor pull_resistor_4 (.node(controlled_buffer_13_out));
  Pull_Resistor pull_resistor_5 (.node(controlled_buffer_14_out));
  Pull_Resistor pull_resistor_6 (.node(controlled_buffer_15_out));
  Pull_Resistor pull_resistor_7 (.node(controlled_buffer_16_out));
  Pull_Resistor pull_resistor_8 (.node(controlled_buffer_17_out));
  Pull_Resistor pull_resistor_9 (.node(controlled_buffer_18_out));
  Pull_Resistor pull_resistor_10 (.node(controlled_buffer_19_out));
  xnor xnor_1 (xnor_1_out, SecondaryBuffer[0], Accumulator[0]);
  xnor xnor_2 (xnor_2_out, SecondaryBuffer[1], Accumulator[1]);
  xnor xnor_3 (xnor_3_out, SecondaryBuffer[2], Accumulator[2]);
  xnor xnor_4 (xnor_4_out, SecondaryBuffer[3], Accumulator[3]);
  xnor xnor_5 (xnor_5_out, SecondaryBuffer[4], Accumulator[4]);
  xnor xnor_6 (xnor_6_out, SecondaryBuffer[5], Accumulator[5]);
  xnor xnor_7 (xnor_7_out, SecondaryBuffer[6], Accumulator[6]);
  xnor xnor_8 (xnor_8_out, SecondaryBuffer[7], Accumulator[7]);
  nor nor_1 (Zero, Accumulator[0], Accumulator[1], Accumulator[2], Accumulator[3], Accumulator[4], Accumulator[5], Accumulator[6], Accumulator[7]);
  or or_3 (or_3_out, controlled_buffer_10_out, controlled_buffer_13_out, controlled_buffer_14_out, controlled_buffer_15_out, controlled_buffer_16_out, controlled_buffer_17_out, controlled_buffer_18_out, controlled_buffer_19_out);
  not not_14 (not_14_out, or_3_out);
  assign ConditionalResult = and_8_out ? or_3_out : 1'bz;  // Controlled_Buffer controlled_buffer_22
  and and_8 (and_8_out, ucf, not_16_out);
  not not_15 (nInst0, Inst0);
  and and_9 (and_9_out, ucf, Condition[0]);
  assign ConditionalResult = and_9_out ? not_14_out : 1'bz;  // Controlled_Buffer controlled_buffer_23
  Pull_Resistor pull_resistor_11 (.node(ConditionalResult));
  not not_16 (not_16_out, Condition[0]);
  and and_10 (Equal, xnor_1_out, xnor_2_out, xnor_3_out, xnor_4_out, xnor_5_out, xnor_6_out, xnor_7_out, xnor_8_out);
  // also tied to GND on the sheet: {n74138_1_pin4, n74138_1_pin5}
  // also tied to VCC on the sheet: n74138_1_pin6

  // Other names for the same wires on the sheet: Databus12[7:0] = Databus; Memory[7:0] = Databus;
  //   Sign = Accumulator[7]; Dev0 = Device0; Dev1 = Device1; Dev2 = Device2; Dev3 = Device3; HALT = in_4;
  //   PrimaryBuffer[7:0] = {Instruction, Inst0, Condition}; Instruction[0] = Inst0; RES = in_6; RESET = in_2

  // Notes on the sheet:
  //   contents of rom_1 (hex, n*v repeats v):
  //   12 e 14 e 80 11*0 12 e 41 e 80 11*0 12 e 13 e 5 54 80 9*0 12 e 13 e 5 54 80 9*0 12 e d e 80 11*0 12
  //   e e 80 12*0 12 e 13 36 80 11*0 12 e 13 e 36 80 10*0 12 e 13 e 67 36 14 76 80 7*0 12 e 13 e 67 36 41
  //   76 80 7*0 12 e 13 e 67 36 13 5 54 76 80 5*0 12 e 13 e 67 36 13 5 54 76 80 5*0 12 d e 80 12*0 12 e 13
  //   e 67 36 71 e f1 76 80 5*0 12 e 13 67 26 19 e 13 36 80 6*0 12 e 13 67 26 19 e 13 36 80
  //   This is basically a Multiplexer
endmodule
